# Fritzing sketch B737_Overhead_AFT (saved by Fritzing 0.9.10b)

parts:
  DM13A = MAX7219 [package=dil24]  # not connected
  RSC_Master_Board1 = Arduino Mega 2560 (Rev3)
  Mux = Analog Digital MUX Breakout
  S1 = NKK M2032SS1W01 3PDT Toggle Switch [part_number=M2032SS1W03 package=THT]  # not connected
  S2 = NKK M2032SS1W01 3PDT Toggle Switch [part_number=M2032SS1W03 package=THT]  # not connected
  S3 = NKK M2032SS1W01 3PDT Toggle Switch [part_number=M2032SS1W03 package=THT]  # not connected
  S4 = NKK M2032SS1W01 3PDT Toggle Switch [part_number=M2032SS1W03 package=THT]  # not connected
  S5 = Momentary Switch [package=ksa_sealed_tac_switch]  # not connected
  S6 = Momentary Switch [package=ksa_sealed_tac_switch]  # not connected
  S7 = Momentary Switch [package=ksa_sealed_tac_switch]  # not connected
  S8 = Momentary Switch [package=ksa_sealed_tac_switch]  # not connected
  S9 = NKK M2032SS1W01 3PDT Toggle Switch [part_number=M2032SS1W03 package=THT]  # not connected
  switch1 = Rotary_Switch_12x1  # not connected
  switch2 = Rotary_Switch_12x1  # not connected
  switch3 = Rotary_Switch_12x1  # not connected
  S10 = Momentary Switch [package=ksa_sealed_tac_switch]  # not connected
  S11 = Momentary Switch [package=ksa_sealed_tac_switch]  # not connected
  S12 = Momentary Switch [package=ksa_sealed_tac_switch]  # not connected
  LED1 = smd LED [color="Orange (620nm)" package="0805 [SMD]"]  # not connected
  LED2 = smd LED [color="Orange (620nm)" package="0805 [SMD]"]  # not connected
  LED3 = smd LED [color="Orange (620nm)" package="0805 [SMD]"]  # not connected
  LED4 = smd LED [color="Orange (620nm)" package="0805 [SMD]"]  # not connected
  LED5 = smd LED [color="Orange (620nm)" package="0805 [SMD]"]  # not connected
  LED6 = smd LED [color="Orange (620nm)" package="0805 [SMD]"]  # not connected
  LED7 = smd LED [color="Orange (620nm)" package="0805 [SMD]"]  # not connected
  LED8 = smd LED [color="Orange (620nm)" package="0805 [SMD]"]  # not connected
  LED9 = smd LED [color="Orange (620nm)" package="0805 [SMD]"]  # not connected
  LED10 = smd LED [color="Orange (620nm)" package="0805 [SMD]"]  # not connected
  LED11 = smd LED [color="Orange (620nm)" package="0805 [SMD]"]  # not connected
  LED12 = smd LED [color="Orange (620nm)" package="0805 [SMD]"]  # not connected
  LED13 = smd LED [color="Orange (620nm)" package="0805 [SMD]"]  # not connected
  LED14 = smd LED [color="Orange (620nm)" package="0805 [SMD]"]  # not connected
  LED15 = smd LED [color="Orange (620nm)" package="0805 [SMD]"]  # not connected
  LED16 = smd LED [color="Orange (620nm)" package="0805 [SMD]"]  # not connected
  LED17 = smd LED [color="Green (570nm)" package="0805 [SMD]"]  # not connected
  LED18 = smd LED [color="Green (570nm)" package="0805 [SMD]"]  # not connected
  LED19 = smd LED [color="Green (570nm)" package="0805 [SMD]"]  # not connected
  LED20 = smd LED [color="Green (570nm)" package="0805 [SMD]"]  # not connected
  LED21 = smd LED [color="Green (570nm)" package="0805 [SMD]"]  # not connected
  LED22 = smd LED [color="Green (570nm)" package="0805 [SMD]"]  # not connected
  LED23 = smd LED [color="Green (570nm)" package="0805 [SMD]"]  # not connected
  LED24 = smd LED [color="Green (570nm)" package="0805 [SMD]"]  # not connected
  LED25 = smd LED [color="Red (660nm)" package="0805 [SMD]"]  # not connected
  LED26 = smd LED [color="Red (660nm)" package="0805 [SMD]"]  # not connected
  LED27 = smd LED [color="White (4500K)" package="0805 [SMD]"]  # not connected
  LED28 = smd LED [color="White (4500K)" package="0805 [SMD]"]  # not connected
  LED29 = smd LED [color="Orange (620nm)" package="0805 [SMD]"]  # not connected
  LED30 = smd LED [color="Orange (620nm)" package="0805 [SMD]"]  # not connected
  S13 = NKK M2032SS1W01 3PDT Toggle Switch [part_number=M2032SS1W03 package=THT]  # not connected
  DM13A1 = MAX7219 [package=dil24]  # not connected
  Mux_2 = Analog Digital MUX Breakout
  J1 = Camdenboss CTB0158-6 [part_number=CTB0158-6 package=THT]  # not connected
  Common_GND = Camdenboss CTB0158-4 [part_number=CTB0158-4 package=THT]
  R1 = Resistor [tolerance=±5% resistance=220 package="2512 [SMD]"]
  R2 = Resistor [tolerance=±5% resistance=220 package="2512 [SMD]"]

nets:
  VCC: RSC_Master_Board1.5V, Mux.VCC, Mux_2.VCC, R1.Pin_1, R2.Pin_1
  N1: RSC_Master_Board1.GND, Common_GND.pin2
  GND: Mux.GND, Mux.EN, Mux_2.GND, Mux_2.EN, Common_GND.pin1
  N2: Mux.S0, Mux_2.S0
  N3: Mux.S1, Mux_2.S1
  N4: Mux.S2, Mux_2.S2
  N5: Mux.S3, Mux_2.S3
  N6: Mux.SIG, R1.Pin_0
  N7: Mux_2.SIG, R2.Pin_0

notes:
  Mach_Warn_Test(2)
  Speed_Warn_Test(1)
  Stall_Warn_Test_R(2)
  Stall_Warn_Test(1)
  signal - pin 30 arduino
  signal - pin 31 arduino
  Flight_Rec_Test
  Oxy_pass_sw
  pin 22 arduino
  pin 23 arduino
  pin 24 arduino
  pin 25 arduino
  VCC - Arduino
  EEC_Eng_R
  EEC_Eng_L
  ELT_ARM
  IRS_Data_Sel
  IRS_Sys_Sel
  IRS_L_Mode
  IRS_R_Mode

custom parts:
  NKK M2032SS1W01 3PDT Toggle Switch: NKK M2032SS1W01 3PDT Toggle Switch This switch has three poles and two position (Jan 2022 replace pads in pcb with pads with holes)
