# Fritzing sketch B737_Overhead_Panel_with_switches (saved by Fritzing 0.9.10b)

parts:
  RSC_Master_Board = Arduino Mega 2560 (Rev3)
  Mux4 = Analog Digital MUX Breakout
  Mux3 = Analog Digital MUX Breakout
  Mux2 = Analog Digital MUX Breakout
  Mux1 = Analog Digital MUX Breakout
  S1 = Taiway 100-SP-X-T1 SPDT Miniature Toggle Switch [part_number=100-SP-X-T1-0-0-B1-M2 package=THT]
  S2 = Taiway 100-SP-X-T1 SPDT Miniature Toggle Switch [part_number=100-SP-X-T1-0-0-B1-M2 package=THT]
  S3 = Taiway 100-SP-X-T1 SPDT Miniature Toggle Switch [part_number=100-SP-X-T1-0-0-B1-M2 package=THT]
  S4 = Taiway 100-SP-X-T1 SPDT Miniature Toggle Switch [part_number=100-SP-X-T1-0-0-B1-M2 package=THT]
  S5 = Taiway 100-SP-X-T1 SPDT Miniature Toggle Switch [part_number=100-SP-X-T1-0-0-B1-M2 package=THT]
  S6 = Taiway 100-SP-X-T1 SPDT Miniature Toggle Switch [part_number=100-SP-X-T1-0-0-B1-M2 package=THT]
  S7 = Taiway 100-SP-X-T1 SPDT Miniature Toggle Switch [part_number=100-SP-X-T1-0-0-B1-M2 package=THT]
  S8 = Taiway 100-SP-X-T1 SPDT Miniature Toggle Switch [part_number=100-SP-X-T1-0-0-B1-M2 package=THT]
  S9 = Taiway 100-SP-X-T1 SPDT Miniature Toggle Switch [part_number=100-SP-X-T1-0-0-B1-M2 package=THT]
  S10 = Taiway 100-SP-X-T1 SPDT Miniature Toggle Switch [part_number=100-SP-X-T1-0-0-B1-M2 package=THT]
  S11 = Taiway 100-SP-X-T1 SPDT Miniature Toggle Switch [part_number=100-SP-X-T1-0-0-B1-M2 package=THT]
  S12 = Taiway 100-SP-X-T1 SPDT Miniature Toggle Switch [part_number=100-SP-X-T1-0-0-B1-M2 package=THT]
  S13 = Taiway 100-SP-X-T1 SPDT Miniature Toggle Switch [part_number=100-SP-X-T1-0-0-B1-M2 package=THT]
  S14 = Taiway 100-SP-X-T1 SPDT Miniature Toggle Switch [part_number=100-SP-X-T1-0-0-B1-M2 package=THT]
  S15 = Taiway 100-SP-X-T1 SPDT Miniature Toggle Switch [part_number=100-SP-X-T1-0-0-B1-M2 package=THT]
  S16 = Taiway 100-SP-X-T1 SPDT Miniature Toggle Switch [part_number=100-SP-X-T1-0-0-B1-M2 package=THT]
  S17 = Taiway 100-SP-X-T1 SPDT Miniature Toggle Switch [part_number=100-SP-X-T1-0-0-B1-M2 package=THT]
  S18 = Taiway 100-SP-X-T1 SPDT Miniature Toggle Switch [part_number=100-SP-X-T1-0-0-B1-M2 package=THT]
  S19 = Taiway 100-SP-X-T1 SPDT Miniature Toggle Switch [part_number=100-SP-X-T1-0-0-B1-M2 package=THT]
  S20 = Taiway 100-SP-X-T1 SPDT Miniature Toggle Switch [part_number=100-SP-X-T1-0-0-B1-M2 package=THT]
  S21 = Taiway 100-SP-X-T1 SPDT Miniature Toggle Switch [part_number=100-SP-X-T1-0-0-B1-M2 package=THT]
  S22 = Taiway 100-SP-X-T1 SPDT Miniature Toggle Switch [part_number=100-SP-X-T1-0-0-B1-M2 package=THT]
  S23 = Taiway 100-SP-X-T1 SPDT Miniature Toggle Switch [part_number=100-SP-X-T1-0-0-B1-M2 package=THT]
  L1 = Solenoid  # not connected
  S24 = Taiway 100-SP-X-T1 SPDT Miniature Toggle Switch [part_number=100-SP-X-T1-0-0-B1-M2 package=THT]
  S25 = Momentary Switch [package=ksa_sealed_tac_switch]
  S26 = Taiway 100-SP-X-T1 SPDT Miniature Toggle Switch [part_number=100-SP-X-T1-0-0-B1-M2 package=THT]
  S27 = Momentary Switch [package=ksa_sealed_tac_switch]
  S28 = Momentary Switch [package=ksa_sealed_tac_switch]
  S29 = Taiway 100-SP-X-T1 SPDT Miniature Toggle Switch [part_number=100-SP-X-T1-0-0-B1-M2 package=THT]
  S30 = Momentary Switch [package=ksa_sealed_tac_switch]
  S32 = Momentary Switch [package=ksa_sealed_tac_switch]
  S33 = Momentary Switch [package=ksa_sealed_tac_switch]
  switch1 = Rotary_Switch_12x1  # not connected
  S34 = Taiway 100-SP-X-T1 SPDT Miniature Toggle Switch [part_number=100-SP-X-T1-0-0-B1-M2 package=THT]
  switch2 = Rotary_Switch_12x1  # not connected
  switch3 = Rotary_Switch_12x1  # not connected
  switch4 = Rotary_Switch_12x1  # not connected
  S35 = Taiway 100-SP-X-T1 SPDT Miniature Toggle Switch [part_number=100-SP-X-T1-0-0-B1-M2 package=THT]
  S36 = Taiway 100-SP-X-T1 SPDT Miniature Toggle Switch [part_number=100-SP-X-T1-0-0-B1-M2 package=THT]
  S37 = Taiway 100-SP-X-T1 SPDT Miniature Toggle Switch [part_number=100-SP-X-T1-0-0-B1-M2 package=THT]
  S38 = Taiway 100-SP-X-T1 SPDT Miniature Toggle Switch [part_number=100-SP-X-T1-0-0-B1-M2 package=THT]
  S39 = Taiway 100-SP-X-T1 SPDT Miniature Toggle Switch [part_number=100-SP-X-T1-0-0-B1-M2 package=THT]
  S40 = Taiway 100-SP-X-T1 SPDT Miniature Toggle Switch [part_number=100-SP-X-T1-0-0-B1-M2 package=THT]
  S41 = Momentary Switch [package=ksa_sealed_tac_switch]
  S42 = Taiway 100-SP-X-T1 SPDT Miniature Toggle Switch [part_number=100-SP-X-T1-0-0-B1-M2 package=THT]
  S43 = Momentary Switch [package=ksa_sealed_tac_switch]
  S44 = Momentary Switch [package=ksa_sealed_tac_switch]
  S45 = Taiway 100-SP-X-T1 SPDT Miniature Toggle Switch [part_number=100-SP-X-T1-0-0-B1-M2 package=THT]
  S46 = Taiway 100-SP-X-T1 SPDT Miniature Toggle Switch [part_number=100-SP-X-T1-0-0-B1-M2 package=THT]
  S47 = Taiway 100-SP-X-T1 SPDT Miniature Toggle Switch [part_number=100-SP-X-T1-0-0-B1-M2 package=THT]
  switch5 = Rotary_Switch_12x1  # not connected
  switch6 = Rotary_Switch_12x1  # not connected
  switch7 = Rotary_Switch_12x1  # not connected
  switch8 = Rotary_Switch_12x1  # not connected
  S48 = Taiway 100-SP-X-T1 SPDT Miniature Toggle Switch [part_number=100-SP-X-T1-0-0-B1-M2 package=THT]
  S49 = Taiway 100-SP-X-T1 SPDT Miniature Toggle Switch [part_number=100-SP-X-T1-0-0-B1-M2 package=THT]
  S50 = Taiway 100-SP-X-T1 SPDT Miniature Toggle Switch [part_number=100-SP-X-T1-0-0-B1-M2 package=THT]
  S51 = Taiway 100-SP-X-T1 SPDT Miniature Toggle Switch [part_number=100-SP-X-T1-0-0-B1-M2 package=THT]
  S52 = Taiway 100-SP-X-T1 SPDT Miniature Toggle Switch [part_number=100-SP-X-T1-0-0-B1-M2 package=THT]
  S53 = Taiway 100-SP-X-T1 SPDT Miniature Toggle Switch [part_number=100-SP-X-T1-0-0-B1-M2 package=THT]
  S54 = Taiway 100-SP-X-T1 SPDT Miniature Toggle Switch [part_number=100-SP-X-T1-0-0-B1-M2 package=THT]
  S55 = Taiway 100-SP-X-T1 SPDT Miniature Toggle Switch [part_number=100-SP-X-T1-0-0-B1-M2 package=THT]
  S56 = Taiway 100-SP-X-T1 SPDT Miniature Toggle Switch [part_number=100-SP-X-T1-0-0-B1-M2 package=THT]
  S57 = Taiway 100-SP-X-T1 SPDT Miniature Toggle Switch [part_number=100-SP-X-T1-0-0-B1-M2 package=THT]
  S58 = Taiway 100-SP-X-T1 SPDT Miniature Toggle Switch [part_number=100-SP-X-T1-0-0-B1-M2 package=THT]
  S59 = Taiway 100-SP-X-T1 SPDT Miniature Toggle Switch [part_number=100-SP-X-T1-0-0-B1-M2 package=THT]
  S60 = Momentary Switch [package=ksa_sealed_tac_switch]
  S61 = Taiway 100-SP-X-T1 SPDT Miniature Toggle Switch [part_number=100-SP-X-T1-0-0-B1-M2 package=THT]
  S62 = Taiway 100-SP-X-T1 SPDT Miniature Toggle Switch [part_number=100-SP-X-T1-0-0-B1-M2 package=THT]
  S63 = Taiway 100-SP-X-T1 SPDT Miniature Toggle Switch [part_number=100-SP-X-T1-0-0-B1-M2 package=THT]
  S64 = Taiway 100-SP-X-T1 SPDT Miniature Toggle Switch [part_number=100-SP-X-T1-0-0-B1-M2 package=THT]
  S65 = Taiway 100-SP-X-T1 SPDT Miniature Toggle Switch [part_number=100-SP-X-T1-0-0-B1-M2 package=THT]
  S66 = Taiway 100-SP-X-T1 SPDT Miniature Toggle Switch [part_number=100-SP-X-T1-0-0-B1-M2 package=THT]
  S67 = Taiway 100-SP-X-T1 SPDT Miniature Toggle Switch [part_number=100-SP-X-T1-0-0-B1-M2 package=THT]
  switch9 = Rotary_Switch_12x1  # not connected
  S68 = Taiway 100-SP-X-T1 SPDT Miniature Toggle Switch [part_number=100-SP-X-T1-0-0-B1-M2 package=THT]
  S69 = Taiway 100-SP-X-T1 SPDT Miniature Toggle Switch [part_number=100-SP-X-T1-0-0-B1-M2 package=THT]
  S70 = Taiway 100-SP-X-T1 SPDT Miniature Toggle Switch [part_number=100-SP-X-T1-0-0-B1-M2 package=THT]
  S71 = Taiway 100-SP-X-T1 SPDT Miniature Toggle Switch [part_number=100-SP-X-T1-0-0-B1-M2 package=THT]
  S72 = Taiway 100-SP-X-T1 SPDT Miniature Toggle Switch [part_number=100-SP-X-T1-0-0-B1-M2 package=THT]
  S73 = Taiway 100-SP-X-T1 SPDT Miniature Toggle Switch [part_number=100-SP-X-T1-0-0-B1-M2 package=THT]
  S74 = Taiway 100-SP-X-T1 SPDT Miniature Toggle Switch [part_number=100-SP-X-T1-0-0-B1-M2 package=THT]
  S75 = Taiway 100-SP-X-T1 SPDT Miniature Toggle Switch [part_number=100-SP-X-T1-0-0-B1-M2 package=THT]
  S76 = Taiway 100-SP-X-T1 SPDT Miniature Toggle Switch [part_number=100-SP-X-T1-0-0-B1-M2 package=THT]
  S77 = Momentary Switch [package=ksa_sealed_tac_switch]
  S78 = Momentary Switch [package=ksa_sealed_tac_switch]
  switch10 = Rotary_Switch_12x1  # not connected
  switch11 = Rotary_Switch_12x1  # not connected
  switch12 = Rotary_Switch_12x1  # not connected
  switch13 = Rotary_Switch_12x1  # not connected
  switch14 = Rotary_Switch_12x1  # not connected
  S79 = Taiway 100-SP-X-T1 SPDT Miniature Toggle Switch [part_number=100-SP-X-T1-0-0-B1-M2 package=THT]
  S31 = Momentary Switch [package=ksa_sealed_tac_switch]
  S80 = Momentary Switch [package=ksa_sealed_tac_switch]
  GND = STARBOARD_GND [package=starboard_ground_small]
  GND1 = STARBOARD_GND [package=starboard_ground_small]
  Mux5 = Analog Digital MUX Breakout
  Mux6 = Analog Digital MUX Breakout
  Mux7 = Analog Digital MUX Breakout
  +5V = STARBOARD_GND [package=starboard_ground_wide]

nets:
  GND: RSC_Master_Board.GND, Mux4.GND, Mux4.EN, Mux3.GND, Mux3.EN, Mux2.GND, Mux2.EN, Mux1.GND, Mux1.EN, S1.COM, S2.COM, S3.L1, S4.COM, S5.COM, S6.COM, S7.COM, S8.COM, S9.COM, S10.L1, S11.L1, S12.L1, S13.L1, S14.L1, S15.L1, S16.L1, S17.COM, S18.COM, S19.COM, S20.L1, S21.L1, S22.L1, S23.L1, S24.L1, S25.1, S26.COM, S27.1, S28.1, S29.L2, S30.1, S32.1, S33.1, S34.COM, S43.1, S44.1, S45.L1, S46.L1, S47.L1, S48.L2, S49.L2, S50.COM, S51.COM, S52.COM, S31.1, GND.MOUNT
  VCC: RSC_Master_Board.5V, Mux4.VCC, Mux3.VCC, Mux2.VCC, Mux1.VCC, +5V.MOUNT
  N1: RSC_Master_Board.D22, Mux4.S0, Mux3.S0, Mux2.S0, Mux1.S0
  N2: RSC_Master_Board.D23, Mux4.S1, Mux3.S1, Mux2.S1, Mux1.S1
  N3: RSC_Master_Board.D24, Mux4.S2, Mux3.S2, Mux2.S2, Mux1.S2
  N4: RSC_Master_Board.D25, Mux4.S3, Mux3.S3, Mux2.S3, Mux1.S3
  N5: RSC_Master_Board.D38, Mux1.SIG
  N6: RSC_Master_Board.D39, Mux2.SIG
  N7: RSC_Master_Board.D40, Mux3.SIG
  N8: RSC_Master_Board.D41, Mux4.SIG
  N9: Mux4.C0, S33.3
  N10: Mux4.C1, S33.4
  N11: Mux4.C2, S22.L2
  N12: Mux4.C3, S23.L2
  N13: Mux4.C4, S34.L1
  N14: Mux4.C5, S34.L2
  N15: Mux4.C6, S48.L1
  N16: Mux4.C7, S49.L1
  N17: Mux4.C8, S50.L1
  N18: Mux4.C9, S50.L2
  N19: Mux4.C10, S51.L1
  N20: Mux4.C11, S51.L2
  N21: Mux4.C12, S52.L1
  N22: Mux4.C13, S52.L2
  N23: Mux4.C14, S44.3
  N24: Mux4.C15, S43.3
  N25: Mux3.C0, S45.L2
  N26: Mux3.C1, S46.L2
  N27: Mux3.C2, S47.L2
  N28: Mux3.C3, S26.L2
  N29: Mux3.C4, S26.L1
  N30: Mux3.C5, S27.3
  N31: Mux3.C6, S28.3
  N32: Mux3.C7, S25.3
  N33: Mux3.C8, S25.4
  N34: Mux3.C9, S29.L1
  N35: Mux3.C10, S30.3
  N36: Mux3.C11, S30.4
  N37: Mux3.C12, S31.3
  N38: Mux3.C13, S31.4
  N39: Mux3.C14, S32.3
  N40: Mux3.C15, S32.4
  N41: Mux2.C0, S9.L2
  N42: Mux2.C1, S9.L1
  N43: Mux2.C2, S10.L2
  N44: Mux2.C3, S11.L2
  N45: Mux2.C4, S12.L2
  N46: Mux2.C5, S13.L2
  N47: Mux2.C6, S14.L2
  N48: Mux2.C7, S15.L2
  N49: Mux2.C8, S16.L2
  N50: Mux2.C9, S17.L1
  N51: Mux2.C10, S17.L2
  N52: Mux2.C11, S18.L1
  N53: Mux2.C12, S18.L2
  N54: Mux2.C13, S19.L2
  N55: Mux2.C14, S20.L2
  N56: Mux2.C15, S21.L2
  N57: Mux1.C0, S1.L1
  N58: Mux1.C1, S1.L2
  N59: Mux1.C2, S2.L1
  N60: Mux1.C3, S2.L2
  N61: Mux1.C4, S3.L2
  N62: Mux1.C5, S4.L1
  N63: Mux1.C6, S4.L2
  N64: Mux1.C7, S24.L2
  N65: Mux1.C8, S5.L2
  N66: Mux1.C9, S5.L1
  N67: Mux1.C10, S6.L2
  N68: Mux1.C11, S6.L1
  N69: Mux1.C12, S7.L2
  N70: Mux1.C13, S7.L1
  N71: Mux1.C14, S8.L2
  N72: Mux1.C15, S8.L1
  N73: S35.COM, S36.L1, S37.COM, S38.L1, S39.L1, S40.L1, S41.1, S42.L1, S53.L1, S54.L1, S55.COM, S56.L1, S57.L1, S58.L1, S59.L1, S60.1, S61.L1, S62.L1, S63.L1, S64.L1, S65.L1, S66.L1, S67.L1, S68.L1, S69.L1, S70.L1, S71.COM, S72.L1, S73.L1, S74.L1, S75.L1, S76.L1, S77.1, S78.1, S79.COM, S80.1, GND1.MOUNT
  N74: S35.L1, Mux7.C11
  N75: S35.L2, Mux7.C10
  N76: S36.L2, Mux7.C4
  N77: S37.L1, Mux7.C6
  N78: S37.L2, Mux7.C5
  N79: S38.L2, Mux7.C7
  N80: S39.L2, Mux7.C8
  N81: S40.L2, Mux7.C9
  N82: S41.4, Mux7.C2
  N83: S42.L2, Mux7.C3
  N84: S53.L2, Mux5.C0
  N85: S54.L2, Mux5.C1
  N86: S55.L1, Mux5.C3
  N87: S55.L2, Mux5.C2
  N88: S56.L2, Mux5.C4
  N89: S57.L2, Mux5.C5
  N90: S58.L2, Mux5.C8
  N91: S59.L2, Mux5.C7
  N92: S60.4, Mux5.C9
  N93: S61.L2, Mux5.C10
  N94: S62.L2, Mux5.C11
  N95: S63.L2, Mux5.C12
  N96: S64.L2, Mux6.C10
  N97: S65.L2, Mux6.C11
  N98: S66.L2, Mux6.C12
  N99: S67.L2, Mux6.C13
  N100: S68.L2, Mux5.C6
  N101: S69.COM, Mux6.C1
  N102: S69.L2, Mux6.C0
  N103: S70.COM, Mux6.C3
  N104: S70.L2, Mux6.C2
  N105: S71.L1, Mux6.C5
  N106: S71.L2, Mux6.C4
  N107: S72.L2, Mux5.C13
  N108: S73.L2, Mux5.C14
  N109: S74.L2, Mux6.C8
  N110: S75.L2, Mux6.C7
  N111: S76.L2, Mux6.C6
  N112: S77.4, Mux6.C9
  N113: S78.4, Mux5.C15
  N114: S79.L1, Mux6.C15
  N115: S79.L2, Mux6.C14
  N116: S80.3, Mux7.C1
  N117: S80.4, Mux7.C0
